# Fritzing sketch base-BistratoV3.2 (saved by Fritzing 0.9.3b)
circuit board: 6.9215cm x 5.33756cm
breadboards: 1

parts:
  J3 = female pin header, 4 pins [form="♀ (female)"]
  R3 = Resistor [tolerance=±5% resistance=220 package=THT]
  S2 = SWITCH-MOMENTARY-2 [package=tactile-pth]
  S1 = SWITCH-MOMENTARY-2 [package=tactile-pth]
  Componente3 = Arduino Uno (Rev3)
  Componente2 = NRF24L01+ Breakout Board
  LED5 = LED - 3mm [color="Red (633nm)" package="3 mm [THT]"]
  R2 = Resistor [tolerance=±5% resistance=220 package=THT]
  LED6 = LED - 3mm [color="Green (565nm)" package="3 mm [THT]"]
  Q2 = NPN-Transistor [package="TO92 [THT]"]
  K1 = Relay [part_number=FRS1B-S package=THT]
  D1 = Rectifier Diode [part_number=1N4001 package="300 mil [THT]"]
  J4 = screw terminal, 3 pins
  U3 = Sharp PC817 [package=THT]
  J5 = Screw terminal - 2 pins [package=THT]
  R4 = Resistor [tolerance=±5% resistance=220 package=THT]
  D2 = Rectifier Diode [part_number=1N4001 package="300 mil [THT]"]
  R5 = Resistor [tolerance=±5% resistance=220 package=THT]
  J6 = female pin header, 1 pin [form="♀ (female)"]
  J7 = female pin header, 1 pin [form="♀ (female)"]
  J8 = female pin header, 1 pin [form="♀ (female)"]
  U2 = Voltage Regulator - Variable [package="TO220 [THT]"]
  J9 = female pin header, 1 pin [form="♀ (female)"]
  J10 = female pin header, 1 pin [form="♀ (female)"]
  J11 = female pin header, 1 pin [form="♀ (female)"]
  J12 = female pin header, 1 pin [form="♀ (female)"]
  Tiny_RTC2 = Tiny RTC
  J15 = female pin header, 1 pin [form="♀ (female)"]
  C1 = Electrolytic Capacitor [capacitance=1µF package="100 mil [THT, electrolytic]"]

nets:
  GND: J3.pin1, S2.2, S1.1, Componente3.GND, Componente2.GND, LED5.cathode, LED6.cathode, Q2.E, U3.Pin_3, J7.pin1, U2.ADJ, J9.pin1, Tiny_RTC2.GND, C1.-
  5V: J3.pin2, Componente3.5V, K1.COIL1, D1.cathode, J8.pin1, U2.IN, J10.pin1, Tiny_RTC2.VCC
  N1: J3.pin3, Componente3.A4/SDA, Tiny_RTC2.SDA
  N2: J3.pin4, Componente3.A5/SCL, Tiny_RTC2.SCL, J15.pin1
  N3: R3.Pin_0, Q2.B
  N4: R3.Pin_1, Componente3.A0, R5.Pin_0
  N5: S2.1, Componente3.A2
  N6: S1.2, Componente3.A3
  N7: Componente3.A1, R2.Pin_0
  N8: Componente3.D8, Componente2.MOSI
  N9: Componente3.D9_PWM, Componente2.CS
  N10: Componente3.D12/MISO, J12.pin1
  N11: Componente3.D13/SCK, J11.pin1
  N12: Componente3.D2, U3.Pin_4
  N13: Componente3.D3_PWM, J6.pin1
  N14: Componente3.D5_PWM, Componente2.CE
  N15: Componente3.D6_PWM, Componente2.SCK
  N16: Componente3.D7, Componente2.MISO
  N17: Componente2.VCC, U2.OUT, C1.+
  N18: LED5.anode, R5.Pin_1
  N19: R2.Pin_1, LED6.anode
  N20: Q2.C, K1.COIL2, D1.anode
  N21: K1.A, J4.pin3
  N22: K1.C1, J4.pin2
  N23: K1.B, J4.pin1
  N24: U3.Pin_1, R4.Pin_1
  N25: U3.Pin_2, J5.pin2
  N26: J5.pin1, D2.anode
  N27: R4.Pin_0, D2.cathode

custom parts:
  Tiny RTC: Tiny RTC I2C module DS1370Z RTC and AT24C32 EEPROM
