# Fritzing sketch sensoreV1.0 (saved by Fritzing 0.9.3b)
circuit board: 6cm x 4.5cm
breadboards: 1

parts:
  Part2 = NRF24L01+ Breakout Board
  R1 = Resistor [tolerance=±5% resistance=220 package=THT]
  R2 = Resistor [tolerance=±5% resistance=220 package=THT]
  T1 = TMP36 Temperature Sensor [package="TO92 [THT]"]
  J1 = female pin header, 1 pin [form="♀ (female)"]
  J2 = female pin header, 1 pin [form="♀ (female)"]
  J3 = female pin header, 1 pin [form="♀ (female)"]
  J4 = female pin header, 1 pin [form="♀ (female)"]
  J5 = female pin header, 1 pin [form="♀ (female)"]
  J6 = female pin header, 1 pin [form="♀ (female)"]
  Part4 = Arduino Pro Mini v13
  J7 = female pin header, 1 pin [form="♀ (female)"]
  J8 = female pin header, 1 pin [form="♀ (female)"]
  J9 = female pin header, 1 pin [form="♀ (female)"]
  J10 = female pin header, 1 pin [form="♀ (female)"]
  J11 = female pin header, 1 pin [form="♀ (female)"]
  J12 = female pin header, 1 pin [form="♀ (female)"]
  J13 = female pin header, 1 pin [form="♀ (female)"]
  J14 = female pin header, 1 pin [form="♀ (female)"]
  J15 = female pin header, 1 pin [form="♀ (female)"]
  J16 = female pin header, 1 pin [form="♀ (female)"]
  J17 = female pin header, 1 pin [form="♀ (female)"]
  J18 = female pin header, 1 pin [form="♀ (female)"]
  J20 = female pin header, 1 pin [form="♀ (female)"]
  J21 = female pin header, 1 pin [form="♀ (female)"]
  J22 = female pin header, 1 pin [form="♀ (female)"]
  J23 = female pin header, 1 pin [form="♀ (female)"]
  J24 = female pin header, 1 pin [form="♀ (female)"]

nets:
  GND: Part2.GND, R1.Pin_1, R2.Pin_1, T1.GND, J1.pin1, Part4.GND, J9.pin1, J10.pin1, J20.pin1, J22.pin1, J23.pin1
  VCC: Part2.VCC, T1.+Vs, J2.pin1, J4.pin1, J6.pin1, Part4.VCC, J7.pin1, J8.pin1, J21.pin1, J24.pin1
  N1: Part2.CE, Part4.D4
  N2: Part2.CS, Part4.D5_PWM
  N3: Part2.SCK, Part4.D13/SCK
  N4: Part2.MOSI, Part4.D11_PWM/MOSI
  N5: Part2.MISO, Part4.D12/MISO
  N6: R1.Pin_0, J5.pin1, Part4.D2
  N7: R2.Pin_0, J3.pin1, Part4.D3_PWM
  N8: T1.Vout, Part4.A3
  N9: Part4.A2, J11.pin1
  N10: Part4.A1, J12.pin1
  N11: Part4.A0, J13.pin1
  N12: Part4.D10_PWM/SS, J14.pin1
  N13: Part4.D9_PWM, J15.pin1
  N14: Part4.D8, J16.pin1
  N15: Part4.D7, J17.pin1
  N16: Part4.D6_PWM, J18.pin1

custom parts:
  Arduino Pro Mini v13: It's blue! It's thin! It's the Arduino Pro Mini! SparkFun's minimal design approach to Arduino. This is a 5V Arduino running the 16MHz bootloader. Arduino Pro Mini does not come with connectors populated so that you can solder in any connector or wire with any orientation you need. We recommend first time Arduino users start with the Uno R3. It's a great board that will get you up and running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
